// Logisim project ALU.circ as structural Verilog: 1 circuit, main circuit main
module main (
  input  [3:0] A,
  input  [3:0] B,
  input  [1:0] in_3,
  input  Lbit,
  input  Rbit,
  input  S2,
  input  S1,
  input  S0,
  output [7:0] out_9
);

  wire [3:0] demultiplexer_1_out0, demultiplexer_1_out1, demultiplexer_1_out2, demultiplexer_1_out3,
       demultiplexer_1_out4, demultiplexer_1_out5, demultiplexer_1_out6, demultiplexer_1_out7,
       demultiplexer_2_out0, demultiplexer_2_out1, demultiplexer_2_out2, demultiplexer_2_out3,
       demultiplexer_2_out7, or_1_out, or_2_out, or_3_out;
  wire [7:0] main_1_result, main_2_result, main_3_product, main_4_r, main_5_result;

  Demultiplexer #(.select(3), .width(4), .enable("false")) demultiplexer_1 (
    .out0(demultiplexer_1_out0), .out1(demultiplexer_1_out1), .out2(demultiplexer_1_out2),
    .out3(demultiplexer_1_out3), .out4(demultiplexer_1_out4), .out5(demultiplexer_1_out5),
    .out6(demultiplexer_1_out6), .out7(demultiplexer_1_out7), .in(A), .sel({S2, S1, S0}));
  Demultiplexer #(.select(3), .width(4), .enable("false")) demultiplexer_2 (
    .out0(demultiplexer_2_out0), .out1(demultiplexer_2_out1), .out2(demultiplexer_2_out2),
    .out3(demultiplexer_2_out3), .out7(demultiplexer_2_out7), .in(B), .sel({S2, S1, S0}));  // open: out4, out5, out6
  assign or_1_out = demultiplexer_1_out0 | demultiplexer_1_out1;  // OR_Gate or_1, 4 bits wide
  assign or_2_out = demultiplexer_1_out6 | demultiplexer_1_out5 | demultiplexer_1_out4;  // OR_Gate or_2, 4 bits wide
  assign or_3_out = demultiplexer_2_out0 | demultiplexer_2_out1;  // OR_Gate or_3, 4 bits wide
  divider_main main_1 (.A(demultiplexer_1_out3), .B(demultiplexer_2_out3), .Result(main_1_result));
  addsub_main main_2 (.C_in(S0), .A(or_1_out), .B(or_3_out), .Result(main_2_result));
  multiplier_main main_3 (.A(demultiplexer_1_out2), .B(demultiplexer_2_out2), .Product(main_3_product));
  logic_main main_4 (.Select(in_3), .A(demultiplexer_1_out7), .B(demultiplexer_2_out7), .R(main_4_r));
  shiftLR_main main_5 (.in_1({S1, S0}), .Lbit(Lbit), .A(or_2_out), .Result(main_5_result), .Rbit(Rbit));
  Multiplexer #(.select(3), .width(8), .enable("false")) multiplexer_1 (
    .in0(main_2_result), .in1(main_2_result), .in2(main_3_product), .in3(main_1_result), .in4(main_5_result),
    .in5(main_5_result), .in6(main_5_result), .in7(main_4_r), .out(out_9), .sel({S2, S1, S0}));
endmodule
