// Logisim project Full Adder.circ as structural Verilog: 1 circuit, main circuit main
// fullAdder
module main (
  input  A,
  input  B,
  input  Cin,
  output SUM,
  output CARRY
);

  wire AND1_out, AND2_out, AND3_out;

  xor XOR (SUM, A, B, Cin);
  and AND1 (AND1_out, A, B);
  and AND2 (AND2_out, B, Cin);
  and AND3 (AND3_out, A, Cin);
  or OR (CARRY, AND1_out, AND2_out, AND3_out);

  // Notes on the sheet:
  //   FULL ADDER 
endmodule
