// Logisim project Half Adder.circ as structural Verilog: 1 circuit, main circuit main
// halfAdder
module main (
  input  A,
  input  B,
  output Sum,
  output Carry
);

  xor XOR (Sum, A, B);
  and AND (Carry, A, B);

  // Notes on the sheet:
  //   HALF ADDER
endmodule
