// Logisim project addsub.circ as structural Verilog: 1 circuit, main circuit main
// addSub
module main (
  input  C_in,
  input  [3:0] A,
  input  [3:0] B,
  output [7:0] Result
);

  wire main_1_carry, main_2_carry, main_3_carry, main_4_carry, not_1_out, xor_1_out, xor_2_out, xor_3_out,
       xor_4_out;

  xor xor_1 (xor_1_out, C_in, B[0]);
  xor xor_2 (xor_2_out, C_in, B[1]);
  xor xor_3 (xor_3_out, C_in, B[2]);
  xor xor_4 (xor_4_out, C_in, B[3]);
  Full_Adder_main main_1 (.B(xor_1_out), .SUM(Result[0]), .CARRY(main_1_carry), .A(A[0]), .Cin(C_in));
  Full_Adder_main main_2 (.B(xor_2_out), .SUM(Result[1]), .CARRY(main_2_carry), .A(A[1]), .Cin(main_1_carry));
  Full_Adder_main main_3 (.B(xor_3_out), .SUM(Result[2]), .CARRY(main_3_carry), .A(A[2]), .Cin(main_2_carry));
  Full_Adder_main main_4 (.B(xor_4_out), .SUM(Result[3]), .CARRY(main_4_carry), .A(A[3]), .Cin(main_3_carry));
  not not_1 (not_1_out, main_4_carry);
  xor xor_5 (Result[4], main_4_carry, C_in);
  and and_1 (Result[7], C_in, not_1_out);

  assign Result[6:5] = {2{Result[7]}};
endmodule
