// Logisim project addsub2.circ as structural Verilog: 1 circuit, main circuit main
module main (
  input  C_in,
  input  [3:0] A,
  input  [3:0] B,
  output [7:0] Result
);

  wire and_1_out, and_2_out, and_3_out, and_4_out, and_5_out, and_6_out, and_7_out, and_8_out, not_1_out,
       or_1_out, or_2_out, or_3_out, or_4_out, xor_1_out, xor_2_out, xor_3_out, xor_4_out, xor_5_out,
       xor_6_out, xor_7_out, xor_8_out;

  xor xor_1 (xor_1_out, C_in, B[0]);
  xor xor_2 (xor_2_out, C_in, B[1]);
  xor xor_3 (xor_3_out, C_in, B[2]);
  xor xor_4 (xor_4_out, C_in, B[3]);
  xor xor_5 (xor_5_out, A[0], xor_1_out);
  xor xor_6 (xor_6_out, A[1], xor_2_out);
  xor xor_7 (xor_7_out, A[2], xor_3_out);
  xor xor_8 (xor_8_out, A[3], xor_4_out);
  and and_1 (and_1_out, C_in, xor_5_out);
  and and_2 (and_2_out, A[0], xor_1_out);
  and and_3 (and_3_out, or_1_out, xor_6_out);
  and and_4 (and_4_out, A[1], xor_2_out);
  and and_5 (and_5_out, or_2_out, xor_7_out);
  and and_6 (and_6_out, A[2], xor_3_out);
  and and_7 (and_7_out, or_3_out, xor_8_out);
  and and_8 (and_8_out, A[3], xor_4_out);
  xor xor_9 (Result[0], C_in, xor_5_out);
  xor xor_10 (Result[1], or_1_out, xor_6_out);
  xor xor_11 (Result[2], or_2_out, xor_7_out);
  xor xor_12 (Result[3], or_3_out, xor_8_out);
  or or_1 (or_1_out, and_1_out, and_2_out);
  or or_2 (or_2_out, and_3_out, and_4_out);
  or or_3 (or_3_out, and_5_out, and_6_out);
  or or_4 (or_4_out, and_7_out, and_8_out);
  not not_1 (not_1_out, or_4_out);
  xor xor_13 (Result[4], or_4_out, C_in);
  and and_9 (Result[7], C_in, not_1_out);

  assign Result[6:5] = {2{Result[7]}};
endmodule
