// Logisim project divider.circ as structural Verilog: 1 circuit, main circuit main
// divider
module main (
  input  [3:0] A,
  input  [3:0] B,
  output [7:0] Result
);

  wire main_1_b_prime, main_1_d, main_2_b_prime, main_2_d, main_3_b_prime, main_3_d, main_4_d,
       main_5_b_prime, main_5_cout, main_5_na, main_6_b_prime, main_6_cout, main_6_na, main_7_b_prime,
       main_7_cout, main_7_na, main_8_cout, main_9_b_prime, main_9_cout, main_9_na, main_10_b_prime,
       main_10_cout, main_10_na, main_11_b_prime, main_11_cout, main_11_na, main_12_cout, main_13_b_prime,
       main_13_cout, main_13_na, main_14_b_prime, main_14_cout, main_14_na, main_15_b_prime, main_15_cout,
       main_15_na, main_16_cout, not_1_out, not_2_out, not_3_out, not_4_out;

  not not_1 (not_1_out, B[0]);
  not not_2 (not_2_out, B[1]);
  not not_3 (not_3_out, B[2]);
  not not_4 (not_4_out, B[3]);
  not not_5 (Result[7], main_1_d);
  not not_6 (Result[6], main_2_d);
  not not_7 (Result[5], main_3_d);
  not not_8 (Result[4], main_4_d);
  divisionCell_main main_1 (
    .Cin(main_5_cout), .A(1'b0), .B(not_4_out), .D(main_1_d), .B_prime(main_1_b_prime), .N(main_1_d));  // open: Cout, nA
  divisionCell_main main_2 (
    .Cin(main_6_cout), .A(main_5_na), .B(main_1_b_prime), .D(main_2_d), .B_prime(main_2_b_prime), .N(main_2_d));  // open: Cout, nA
  divisionCell_main main_3 (
    .Cin(main_7_cout), .A(main_6_na), .B(main_2_b_prime), .D(main_3_d), .B_prime(main_3_b_prime), .N(main_3_d));  // open: Cout, nA
  divisionCell_main main_4 (
    .Cin(main_8_cout), .A(main_7_na), .B(main_3_b_prime), .D(main_4_d), .nA(Result[3]), .N(main_4_d));  // open: Cout, B_prime
  divisionCell_main main_5 (
    .Cin(main_9_cout), .A(1'b0), .B(not_3_out), .Cout(main_5_cout), .nA(main_5_na), .B_prime(main_5_b_prime),
    .N(main_1_d));  // open: D
  divisionCell_main main_6 (
    .Cin(main_10_cout), .A(main_9_na), .B(main_5_b_prime), .Cout(main_6_cout), .nA(main_6_na),
    .B_prime(main_6_b_prime), .N(main_2_d));  // open: D
  divisionCell_main main_7 (
    .Cin(main_11_cout), .A(main_10_na), .B(main_6_b_prime), .Cout(main_7_cout), .nA(main_7_na),
    .B_prime(main_7_b_prime), .N(main_3_d));  // open: D
  divisionCell_main main_8 (
    .Cin(main_12_cout), .A(main_11_na), .B(main_7_b_prime), .Cout(main_8_cout), .nA(Result[2]), .N(main_4_d));  // open: D, B_prime
  divisionCell_main main_9 (
    .Cin(main_13_cout), .A(1'b0), .B(not_2_out), .Cout(main_9_cout), .nA(main_9_na),
    .B_prime(main_9_b_prime), .N(main_1_d));  // open: D
  divisionCell_main main_10 (
    .Cin(main_14_cout), .A(main_13_na), .B(main_9_b_prime), .Cout(main_10_cout), .nA(main_10_na),
    .B_prime(main_10_b_prime), .N(main_2_d));  // open: D
  divisionCell_main main_11 (
    .Cin(main_15_cout), .A(main_14_na), .B(main_10_b_prime), .Cout(main_11_cout), .nA(main_11_na),
    .B_prime(main_11_b_prime), .N(main_3_d));  // open: D
  divisionCell_main main_12 (
    .Cin(main_16_cout), .A(main_15_na), .B(main_11_b_prime), .Cout(main_12_cout), .nA(Result[1]), .N(main_4_d));  // open: D, B_prime
  divisionCell_main main_13 (
    .Cin(1'b1), .A(A[3]), .B(not_1_out), .Cout(main_13_cout), .nA(main_13_na), .B_prime(main_13_b_prime),
    .N(main_1_d));  // open: D
  divisionCell_main main_14 (
    .Cin(1'b1), .A(A[2]), .B(main_13_b_prime), .Cout(main_14_cout), .nA(main_14_na),
    .B_prime(main_14_b_prime), .N(main_2_d));  // open: D
  divisionCell_main main_15 (
    .Cin(1'b1), .A(A[1]), .B(main_14_b_prime), .Cout(main_15_cout), .nA(main_15_na),
    .B_prime(main_15_b_prime), .N(main_3_d));  // open: D
  divisionCell_main main_16 (
    .Cin(1'b1), .A(A[0]), .B(main_15_b_prime), .Cout(main_16_cout), .nA(Result[0]), .N(main_4_d));  // open: D, B_prime
endmodule
