// Logisim project divisionCell.circ as structural Verilog: 1 circuit, main circuit main
// cell
module main (
  input  Cin,
  input  A,
  input  B,
  input  N,
  output D,
  output Cout,
  output nA,
  output B_prime
);

  Full_Adder_main main_1 (.B(B), .SUM(D), .CARRY(Cout), .A(A), .Cin(Cin));
  Multiplexer #(.enable("false")) multiplexer_1 (.in0(D), .in1(A), .out(nA), .sel(N));

  assign B_prime = B;
endmodule
