// Logisim project logic.circ as structural Verilog: 1 circuit, main circuit main
// logic
module main (
  input  [3:0] A,
  input  [3:0] B,
  input  [1:0] Select,
  output [7:0] R
);

  wire AND_2_out, AND_3_out, AND_4_out, AND_out, NOT_2_out, NOT_3_out, NOT_4_out, NOT_out, OR_2_out,
       OR_3_out, OR_4_out, OR_out, XOR_2_out, XOR_3_out, XOR_4_out, XOR_out;

  and AND (AND_out, A[0], B[0]);
  or OR (OR_out, A[0], B[0]);
  not NOT (NOT_out, A[0]);
  and AND_2 (AND_2_out, A[1], B[1]);
  or OR_2 (OR_2_out, A[1], B[1]);
  not NOT_2 (NOT_2_out, A[1]);
  and AND_3 (AND_3_out, A[2], B[2]);
  or OR_3 (OR_3_out, A[2], B[2]);
  not NOT_3 (NOT_3_out, A[2]);
  and AND_4 (AND_4_out, A[3], B[3]);
  or OR_4 (OR_4_out, A[3], B[3]);
  not NOT_4 (NOT_4_out, A[3]);
  xor XOR (XOR_out, A[0], B[0]);
  xor XOR_2 (XOR_2_out, A[1], B[1]);
  xor XOR_3 (XOR_3_out, A[2], B[2]);
  xor XOR_4 (XOR_4_out, A[3], B[3]);
  Multiplexer #(.select(2), .enable("false")) multiplexer_1 (
    .in0(AND_out), .in1(OR_out), .in2(NOT_out), .in3(XOR_out), .out(R[0]), .sel(Select));
  Multiplexer #(.select(2), .enable("false")) multiplexer_2 (
    .in0(AND_2_out), .in1(OR_2_out), .in2(NOT_2_out), .in3(XOR_2_out), .out(R[1]), .sel(Select));
  Multiplexer #(.select(2), .enable("false")) multiplexer_3 (
    .in0(AND_3_out), .in1(OR_3_out), .in2(NOT_3_out), .in3(XOR_3_out), .out(R[2]), .sel(Select));
  Multiplexer #(.select(2), .enable("false")) multiplexer_4 (
    .in0(AND_4_out), .in1(OR_4_out), .in2(NOT_4_out), .in3(XOR_4_out), .out(R[3]), .sel(Select));

  assign R[7:4] = 4'b0000;
endmodule
