// Logisim project multiplier.circ as structural Verilog: 1 circuit, main circuit main
// Multiplier
module main (
  input  [3:0] A,
  input  [3:0] B,
  output [7:0] Product
);

  wire and_1_out, and_2_out, and_3_out, and_4_out, and_5_out, and_6_out, and_7_out, and_8_out, and_9_out,
       and_10_out, and_12_out, and_13_out, and_14_out, and_15_out, and_16_out, main_1_carry, main_2_carry,
       main_2_sum, main_3_carry, main_3_sum, main_4_carry, main_5_carry, main_5_sum, main_6_carry,
       main_6_sum, main_7_carry, main_8_carry, main_8_sum, main_9_carry, main_9_sum, main_10_carry,
       main_11_carry;

  and and_1 (and_1_out, A[1], B[0]);
  and and_2 (and_2_out, A[0], B[1]);
  and and_3 (and_3_out, B[1], A[1]);
  and and_4 (and_4_out, B[0], A[2]);
  and and_5 (and_5_out, B[1], A[2]);
  and and_6 (and_6_out, B[0], A[3]);
  Half_Adder_main main_1 (.A(and_1_out), .B(and_2_out), .Sum(Product[1]), .Carry(main_1_carry));
  Half_Adder_main main_2 (.A(and_3_out), .B(and_4_out), .Sum(main_2_sum), .Carry(main_2_carry));
  Half_Adder_main main_3 (.A(and_5_out), .B(and_6_out), .Sum(main_3_sum), .Carry(main_3_carry));
  and and_7 (and_7_out, A[0], B[2]);
  and and_8 (and_8_out, A[1], B[2]);
  and and_9 (and_9_out, B[2], A[2]);
  and and_10 (and_10_out, A[3], B[1]);
  and and_11 (Product[0], A[0], B[0]);
  Full_Adder_main main_4 (.B(and_7_out), .SUM(Product[2]), .CARRY(main_4_carry), .A(main_2_sum), .Cin(main_1_carry));
  Full_Adder_main main_5 (.B(and_8_out), .SUM(main_5_sum), .CARRY(main_5_carry), .A(main_3_sum), .Cin(main_2_carry));
  Full_Adder_main main_6 (.B(and_10_out), .SUM(main_6_sum), .CARRY(main_6_carry), .A(and_9_out), .Cin(main_3_carry));
  and and_12 (and_12_out, A[0], B[3]);
  and and_13 (and_13_out, A[1], B[3]);
  and and_14 (and_14_out, A[2], B[3]);
  and and_15 (and_15_out, B[2], A[3]);
  Full_Adder_main main_7 (.B(and_12_out), .SUM(Product[3]), .CARRY(main_7_carry), .A(main_5_sum), .Cin(main_4_carry));
  Full_Adder_main main_8 (.B(and_13_out), .SUM(main_8_sum), .CARRY(main_8_carry), .A(main_6_sum), .Cin(main_5_carry));
  Full_Adder_main main_9 (.B(and_15_out), .SUM(main_9_sum), .CARRY(main_9_carry), .A(and_14_out), .Cin(main_6_carry));
  and and_16 (and_16_out, A[3], B[3]);
  Half_Adder_main main_10 (.A(main_7_carry), .B(main_8_sum), .Sum(Product[4]), .Carry(main_10_carry));
  Full_Adder_main main_11 (
    .B(main_9_sum), .SUM(Product[5]), .CARRY(main_11_carry), .A(main_8_carry), .Cin(main_10_carry));
  Full_Adder_main main_12 (.B(and_16_out), .SUM(Product[6]), .CARRY(Product[7]), .A(main_9_carry), .Cin(main_11_carry));
endmodule
