// Logisim project shiftLR.circ as structural Verilog: 1 circuit, main circuit main
// Shift
module main (
  input  [1:0] in_1,
  input  Rbit,
  input  Lbit,
  input  [3:0] A,
  output [7:0] Result
);

  wire clock_1_out, multiplexer_1_out, multiplexer_2_out, multiplexer_3_out, multiplexer_4_out,
       multiplexer_5_out, multiplexer_6_out, multiplexer_7_out, multiplexer_8_out;

  Multiplexer #(.select(2), .enable("false")) multiplexer_1 (
    .in0(A[0]), .in1(Result[1]), .in2(Lbit), .in3(Result[0]), .out(multiplexer_1_out), .sel(in_1));
  D_Flip_Flop d_ff_1 (.clk(clock_1_out), .D(multiplexer_1_out), .Q(Result[0]));  // open: Qn, preset, en, reset
  D_Flip_Flop d_ff_2 (.clk(clock_1_out), .D(multiplexer_2_out), .Q(Result[1]));  // open: Qn, preset, en, reset
  Multiplexer #(.select(2), .enable("false")) multiplexer_2 (
    .in0(A[1]), .in1(Result[2]), .in2(Result[0]), .in3(Result[1]), .out(multiplexer_2_out), .sel(in_1));
  D_Flip_Flop d_ff_3 (.clk(clock_1_out), .D(multiplexer_3_out), .Q(Result[2]));  // open: Qn, preset, en, reset
  Multiplexer #(.select(2), .enable("false")) multiplexer_3 (
    .in0(A[2]), .in1(Result[3]), .in2(Result[1]), .in3(Result[2]), .out(multiplexer_3_out), .sel(in_1));
  Multiplexer #(.select(2), .enable("false")) multiplexer_4 (
    .in0(A[3]), .in1(Result[4]), .in2(Result[2]), .in3(Result[3]), .out(multiplexer_4_out), .sel(in_1));
  D_Flip_Flop d_ff_4 (.clk(clock_1_out), .D(multiplexer_4_out), .Q(Result[3]));  // open: Qn, preset, en, reset
  Multiplexer #(.select(2), .enable("false")) multiplexer_5 (
    .in0(1'b0), .in1(Result[5]), .in2(Result[3]), .in3(Result[4]), .out(multiplexer_5_out), .sel(in_1));
  D_Flip_Flop d_ff_5 (.clk(clock_1_out), .D(multiplexer_5_out), .Q(Result[4]));  // open: Qn, preset, en, reset
  Multiplexer #(.select(2), .enable("false")) multiplexer_6 (
    .in0(1'b0), .in1(Result[6]), .in2(Result[4]), .in3(Result[5]), .out(multiplexer_6_out), .sel(in_1));
  D_Flip_Flop d_ff_6 (.clk(clock_1_out), .D(multiplexer_6_out), .Q(Result[5]));  // open: Qn, preset, en, reset
  Multiplexer #(.select(2), .enable("false")) multiplexer_7 (
    .in0(1'b0), .in1(Result[7]), .in2(Result[5]), .in3(Result[6]), .out(multiplexer_7_out), .sel(in_1));
  D_Flip_Flop d_ff_7 (.clk(clock_1_out), .D(multiplexer_7_out), .Q(Result[6]));  // open: Qn, preset, en, reset
  Multiplexer #(.select(2), .enable("false")) multiplexer_8 (
    .in0(1'b0), .in1(Rbit), .in2(Result[6]), .in3(Result[7]), .out(multiplexer_8_out), .sel(in_1));
  D_Flip_Flop d_ff_8 (.clk(clock_1_out), .D(multiplexer_8_out), .Q(Result[7]));  // open: Qn, preset, en, reset
  Clock clock_1 (.out(clock_1_out));
endmodule
